// Logisim project mini_project.circ as structural Verilog: 4 circuits, main circuit main
module main (
  input  RESET,
  output [31:0] out_2
);

  wire A_sel, ALU_b0, ALU_b1, and_1_out, and_2_out, and_3_out, and_4_out, and_9_out, and_10_out, and_11_out,
       and_12_out, and_16_out, B_sel, CLK, comparator_1_eq, comparator_2_eq, comparator_3_eq,
       comparator_4_eq, comparator_5_eq, comparator_7_eq, comparator_8_eq, comparator_9_eq, HLT, IR_act,
       not_1_out, not_2_out, not_3_out, not_4_out, not_5_out, not_6_out, not_7_out, not_8_out, not_9_out,
       not_10_out, not_11_out, not_12_out, not_13_out, not_14_out, not_15_out, not_16_out, not_17_out,
       not_18_out, not_19_out, not_20_out, not_21_out, op_2, op_3, op_4, op_5, or_2_out, or_3_out, PC_act,
       STORE, Write, Y_sel;
  wire [2:0] Stage;
  wire [4:0] R_A, R_Af, R_B, R_Bf, R_C;
  wire [10:0] X_imd;
  wire [15:0] multiplexer_6_out, Rz_q;
  wire [31:0] adder_1_out, alu_1_result, bit_extender_1_out, bit_extender_2_out, demultiplexer_1_out0,
       demultiplexer_1_out1, multiplexer_1_out, multiplexer_2_out, multiplexer_3_out, Ra_q, ram_1_data, Rb_q,
       register_file_1_r_a, register_file_1_r_b, Rm_q, Ry_q;
  wire [31:16] Rz_q_2;
  wire [31:30] IR_q;

  Register #(.width(32)) IR (
    .D(demultiplexer_1_out0), .en(and_1_out), .Q({IR_q, op_2, op_3, op_4, op_5, R_C, R_A, R_B, X_imd}),
    .clk(CLK), .clr(RESET));
  and and_1 (and_1_out, IR_act, not_1_out);
  not not_1 (not_1_out, HLT);
  Comparator #(.width(3)) comparator_1 (.a(Stage), .b(3'b001), .eq(comparator_1_eq));  // open: gt, lt
  Comparator #(.width(3)) comparator_2 (.a(Stage), .b(3'b010), .eq(comparator_2_eq));  // open: gt, lt
  Comparator #(.width(3)) comparator_3 (.a(Stage), .b(3'b011), .eq(comparator_3_eq));  // open: gt, lt
  not not_2 (not_2_out, op_2);
  not not_3 (not_3_out, op_3);
  not not_4 (not_4_out, op_3);
  and and_2 (and_2_out, not_2_out, op_5);
  and and_3 (and_3_out, not_3_out, op_5);
  and and_4 (and_4_out, op_2, not_4_out, op_4);
  Counter #(.width(3), .max('h7), .trigger("falling")) counter_1 (
    .Q(Stage), .clk(CLK), .clr(or_2_out));  // open: load, D, count, carry
  not not_5 (not_5_out, HLT);
  not not_6 (not_6_out, op_3);
  not not_7 (not_7_out, op_3);
  not not_8 (not_8_out, op_4);
  not not_9 (not_9_out, op_3);
  not not_10 (not_10_out, op_5);
  Comparator #(.width(3)) comparator_4 (.a(Stage), .b(3'b000), .eq(comparator_4_eq));  // open: gt, lt
  Register #(.width(32)) Ra (.D(register_file_1_r_a), .en(comparator_1_eq), .Q(Ra_q), .clk(CLK), .clr(RESET));
  Multiplexer #(.width(32)) multiplexer_1 (
    .in0(Ra_q), .in1({32{1'b0}}), .out(multiplexer_1_out), .sel(A_sel));  // open: en
  and and_5 (A_sel, op_2, not_7_out, not_8_out);
  or or_1 (B_sel, and_2_out, and_3_out, and_4_out);
  and and_6 (Y_sel, op_2, not_9_out, op_4, not_10_out);
  not not_11 (not_11_out, Stage[1]);
  or or_2 (or_2_out, and_9_out, RESET);
  and and_7 (PC_act, comparator_4_eq, not_5_out);
  and and_8 (STORE, op_2, not_6_out, op_4, op_5);
  Register_File register_file_1 (
    .I_CLK(CLK), .R_C(Ry_q), .write(and_10_out), .Add_A(R_Af), .Add_B(R_Bf), .Add_C(R_C), .RESET(RESET),
    .R_B(register_file_1_r_b), .R_A(register_file_1_r_a));
  Register #(.width(32)) Rb (.D(register_file_1_r_b), .en(comparator_1_eq), .Q(Rb_q), .clk(CLK), .clr(RESET));
  Multiplexer #(.width(32)) multiplexer_2 (
    .in0(Rb_q), .in1(bit_extender_1_out), .out(multiplexer_2_out), .sel(B_sel));  // open: en
  ALU alu_1 (.In_X(multiplexer_1_out), .In_Y(multiplexer_2_out), .Result(alu_1_result), .SELECT({ALU_b0, ALU_b1}));
  Register #(.width(32)) Rz (.D(alu_1_result), .en(comparator_2_eq), .Q({Rz_q_2, Rz_q}), .clk(CLK), .clr(RESET));
  Multiplexer #(.width(32)) multiplexer_3 (
    .in0({Rz_q_2, Rz_q}), .in1(demultiplexer_1_out1), .out(multiplexer_3_out), .sel(Y_sel));  // open: en
  Register #(.width(32)) Ry (.D(multiplexer_3_out), .en(comparator_3_eq), .Q(Ry_q), .clk(CLK), .clr(RESET));
  and and_9 (and_9_out, Stage[0], not_11_out, Stage[2]);
  Comparator #(.width(3)) comparator_5 (.a(Stage), .b(3'b100), .eq(comparator_5_eq));  // open: gt, lt
  and and_10 (and_10_out, comparator_5_eq, Write);
  not not_12 (not_12_out, HLT);
  assign bit_extender_1_out = {{16{1'b0}}, {R_B, X_imd}};  // Bit_Extender bit_extender_1
  not not_13 (not_13_out, op_2);
  not not_14 (not_14_out, op_3);
  not not_15 (not_15_out, op_4);
  not not_16 (not_16_out, op_5);
  and and_11 (and_11_out, PC_act, not_12_out);
  Register #(.width(32), .trigger("falling")) Rm (.D(Rb_q), .en(comparator_1_eq), .Q(Rm_q), .clk(CLK), .clr(RESET));
  or or_3 (or_3_out, not_15_out, not_16_out);
  not not_17 (not_17_out, op_2);
  not not_18 (not_18_out, op_2);
  not not_19 (not_19_out, op_4);
  not not_20 (not_20_out, op_5);
  Register #(.width(32)) PC (.D(adder_1_out), .en(and_11_out), .Q(out_2), .clk(CLK), .clr(RESET));
  and and_12 (and_12_out, not_14_out, or_3_out);
  and and_13 (ALU_b0, not_17_out, op_3);
  and and_14 (ALU_b1, not_18_out, op_4);
  Comparator #(.width(3)) comparator_6 (.a(Stage), .b(3'b000), .eq(IR_act));  // open: gt, lt
  assign bit_extender_2_out = {{29{1'b0}}, 3'b001};  // Bit_Extender bit_extender_2
  or or_4 (Write, not_13_out, and_12_out);
  and and_15 (HLT, op_2, op_3, not_19_out, not_20_out);
  Multiplexer #(.width(5)) multiplexer_4 (.in0(R_A), .in1(R_C), .out(R_Af), .sel(STORE));  // open: en
  Multiplexer #(.width(5)) multiplexer_5 (.in0(R_B), .in1(R_A), .out(R_Bf), .sel(STORE));  // open: en
  Adder #(.width(32)) adder_1 (.a(bit_extender_2_out), .b(out_2), .out(adder_1_out));  // open: cin, cout
  Multiplexer #(.width(16)) multiplexer_6 (
    .in0(out_2[15:0]), .in1(Rz_q), .out(multiplexer_6_out), .sel(comparator_7_eq));  // open: en
  Clock u_CLK (.out(CLK));
  Comparator #(.width(3)) comparator_7 (.a(Stage), .b(3'b011), .eq(comparator_7_eq));  // open: gt, lt
  RAM #(.addrWidth(16), .dataWidth(32), .bus("separate")) ram_1 (
    .addr(multiplexer_6_out), .din(Rm_q), .data(ram_1_data), .str(and_16_out), .clk(CLK), .ld(not_21_out),
    .clr(RESET));  // open: sel
  Comparator #(.width(3)) comparator_8 (.a(Stage), .b(3'b011), .eq(comparator_8_eq));  // open: gt, lt
  Comparator #(.width(3)) comparator_9 (.a(Stage), .b(3'b011), .eq(comparator_9_eq));  // open: gt, lt
  not not_21 (not_21_out, and_16_out);
  Demultiplexer #(.width(32)) demultiplexer_1 (
    .out0(demultiplexer_1_out0), .out1(demultiplexer_1_out1), .in(ram_1_data), .sel(comparator_9_eq));  // open: en
  and and_16 (and_16_out, comparator_8_eq, STORE);

  // Other names for the same wires on the sheet: X_imd[15:11] = R_B; Reset_ALL = RESET
endmodule

module ALU (
  input  [31:0] In_X,
  input  [31:0] In_Y,
  input  [1:0] SELECT,
  output [31:0] Result
);

  wire [31:0] adder_1_out, and_1_out, or_1_out, subtractor_1_out;

  Adder #(.width(32)) adder_1 (.a(In_X), .b(In_Y), .out(adder_1_out));  // open: cin, cout
  Subtractor #(.width(32)) subtractor_1 (.a(In_X), .b(In_Y), .out(subtractor_1_out));  // open: bin, bout
  assign and_1_out = In_X & In_Y;  // AND_Gate and_1, 32 bits wide
  assign or_1_out = In_X | In_Y;  // OR_Gate or_1, 32 bits wide
  Multiplexer #(.select(2), .width(32)) multiplexer_1 (
    .in0(adder_1_out), .in1(subtractor_1_out), .in2(and_1_out), .in3(or_1_out), .out(Result), .sel(SELECT));  // open: en
endmodule

// out_28
module Register_File (
  input  I_CLK,
  input  RESET,
  input  [31:0] R_C,
  input  write,
  input  [4:0] Add_C,
  input  [4:0] Add_B,
  input  [4:0] Add_A,
  output [31:0] R_B,
  output [31:0] R_A
);

  wire en_1, en_2, en_3, en_4, en_5, en_6, en_7, en_8, en_9, en_10, en_11, en_12, en_13, en_14, en_15, en_16,
       en_17, en_18, en_19, en_20, en_21, en_22, en_23, en_24, en_25, en_26, en_27, en_28, en_29, en_30,
       en_31, en_32;
  wire [31:0] out_1, out_2, out_3, out_4, out_5, out_6, out_7, out_8, out_9, out_10, out_11, out_12, out_13,
       out_14, out_15, out_16, out_17, out_18, out_19, out_20, out_21, out_22, out_23, out_24, out_25,
       out_26, out_27, out_28, out_29, out_30, out_31, out_32;

  Register #(.width(32)) register_1 (.D(R_C), .en(en_1), .Q(out_1), .clk(I_CLK), .clr(RESET));
  Register #(.width(32)) register_2 (.D(R_C), .en(en_9), .Q(out_9), .clk(I_CLK), .clr(RESET));
  Register #(.width(32)) register_3 (.D(R_C), .en(en_17), .Q(out_17), .clk(I_CLK), .clr(RESET));
  Register #(.width(32)) register_4 (.D(R_C), .en(en_25), .Q(out_25), .clk(I_CLK), .clr(RESET));
  Register #(.width(32)) register_5 (.D(R_C), .en(en_2), .Q(out_2), .clk(I_CLK), .clr(RESET));
  Register #(.width(32)) register_6 (.D(R_C), .en(en_10), .Q(out_10), .clk(I_CLK), .clr(RESET));
  Register #(.width(32)) register_7 (.D(R_C), .en(en_18), .Q(out_18), .clk(I_CLK), .clr(RESET));
  Register #(.width(32)) register_8 (.D(R_C), .en(en_26), .Q(out_26), .clk(I_CLK), .clr(RESET));
  Multiplexer #(.select(5), .width(32)) multiplexer_1 (
    .in0(out_1), .in1(out_2), .in2(out_3), .in3(out_4), .in4(out_5), .in5(out_6), .in6(out_7), .in7(out_8),
    .in8(out_9), .in9(out_10), .in10(out_11), .in11(out_12), .in12(out_13), .in13(out_14), .in14(out_15),
    .in15(out_16), .in16(out_17), .in17(out_18), .in18(out_19), .in19(out_20), .in20(out_21), .in21(out_22),
    .in22(out_23), .in23(out_24), .in24(out_25), .in25(out_26), .in26(out_27), .in27(out_28), .in28(out_29),
    .in29(out_30), .in30(out_31), .in31(out_32), .out(R_A), .sel(Add_A));  // open: en
  Register #(.width(32)) register_9 (.D(R_C), .en(en_3), .Q(out_3), .clk(I_CLK), .clr(RESET));
  Register #(.width(32)) register_10 (.D(R_C), .en(en_11), .Q(out_11), .clk(I_CLK), .clr(RESET));
  Register #(.width(32)) register_11 (.D(R_C), .en(en_19), .Q(out_19), .clk(I_CLK), .clr(RESET));
  Register #(.width(32)) register_12 (.D(R_C), .en(en_27), .Q(out_27), .clk(I_CLK), .clr(RESET));
  Register #(.width(32)) register_13 (.D(R_C), .en(en_4), .Q(out_4), .clk(I_CLK), .clr(RESET));
  Register #(.width(32)) register_14 (.D(R_C), .en(en_12), .Q(out_12), .clk(I_CLK), .clr(RESET));
  Register #(.width(32)) register_15 (.D(R_C), .en(en_20), .Q(out_20), .clk(I_CLK), .clr(RESET));
  Register #(.width(32)) register_16 (.D(R_C), .en(en_28), .Q(out_28), .clk(I_CLK), .clr(RESET));
  Register #(.width(32)) register_17 (.D(R_C), .en(en_5), .Q(out_5), .clk(I_CLK), .clr(RESET));
  Register #(.width(32)) register_18 (.D(R_C), .en(en_13), .Q(out_13), .clk(I_CLK), .clr(RESET));
  Register #(.width(32)) register_19 (.D(R_C), .en(en_21), .Q(out_21), .clk(I_CLK), .clr(RESET));
  Register #(.width(32)) register_20 (.D(R_C), .en(en_29), .Q(out_29), .clk(I_CLK), .clr(RESET));
  Register #(.width(32)) register_21 (.D(R_C), .en(en_6), .Q(out_6), .clk(I_CLK), .clr(RESET));
  Register #(.width(32)) register_22 (.D(R_C), .en(en_14), .Q(out_14), .clk(I_CLK), .clr(RESET));
  Register #(.width(32)) register_23 (.D(R_C), .en(en_22), .Q(out_22), .clk(I_CLK), .clr(RESET));
  Register #(.width(32)) register_24 (.D(R_C), .en(en_30), .Q(out_30), .clk(I_CLK), .clr(RESET));
  Multiplexer #(.select(5), .width(32)) multiplexer_2 (
    .in0(out_1), .in1(out_2), .in2(out_3), .in3(out_4), .in4(out_5), .in5(out_6), .in6(out_7), .in7(out_8),
    .in8(out_9), .in9(out_10), .in10(out_11), .in11(out_12), .in12(out_13), .in13(out_14), .in14(out_15),
    .in15(out_16), .in16(out_17), .in17(out_18), .in18(out_19), .in19(out_20), .in20(out_21), .in21(out_22),
    .in22(out_23), .in23(out_24), .in24(out_25), .in25(out_26), .in26(out_27), .in27(out_28), .in28(out_29),
    .in29(out_30), .in30(out_31), .in31(out_32), .out(R_B), .sel(Add_B));  // open: en
  Register #(.width(32)) register_25 (.D(R_C), .en(en_7), .Q(out_7), .clk(I_CLK), .clr(RESET));
  Register #(.width(32)) register_26 (.D(R_C), .en(en_15), .Q(out_15), .clk(I_CLK), .clr(RESET));
  Register #(.width(32)) register_27 (.D(R_C), .en(en_23), .Q(out_23), .clk(I_CLK), .clr(RESET));
  Register #(.width(32)) register_28 (.D(R_C), .en(en_31), .Q(out_31), .clk(I_CLK), .clr(RESET));
  Register #(.width(32)) register_29 (.D(R_C), .en(en_8), .Q(out_8), .clk(I_CLK), .clr(RESET));
  Register #(.width(32)) register_30 (.D(R_C), .en(en_16), .Q(out_16), .clk(I_CLK), .clr(RESET));
  Register #(.width(32)) register_31 (.D(R_C), .en(en_24), .Q(out_24), .clk(I_CLK), .clr(RESET));
  Register #(.width(32)) register_32 (.D(R_C), .en(en_32), .Q(out_32), .clk(I_CLK), .clr(RESET));
  Demultiplexer #(.select(5)) demultiplexer_1 (
    .out0(en_1), .out1(en_2), .out2(en_3), .out3(en_4), .out4(en_5), .out5(en_6), .out6(en_7), .out7(en_8),
    .out8(en_9), .out9(en_10), .out10(en_11), .out11(en_12), .out12(en_13), .out13(en_14), .out14(en_15),
    .out15(en_16), .out16(en_17), .out17(en_18), .out18(en_19), .out19(en_20), .out20(en_21), .out21(en_22),
    .out22(en_23), .out23(en_24), .out24(en_25), .out25(en_26), .out26(en_27), .out27(en_28), .out28(en_29),
    .out29(en_30), .out30(en_31), .out31(en_32), .in(write), .sel(Add_C));  // open: en
endmodule

module prac (
  input  in_1,
  input  in_2,
  input  [31:0] in_3,
  input  [31:0] in_4,
  output [31:0] out_5
);

  ALU alu_1 (.In_X(in_3), .In_Y(in_4), .Result(out_5), .SELECT({in_2, in_1}));

  // Notes on the sheet:
  //   This file is used to try and verify components
endmodule
